# Fritzing sketch turret (saved by Fritzing 1.0.2b)

parts:
  M1 = STM32407VG Discovery
  Pololu_A1 = Pololu A4988 [package=SO16]
  M2 = Stepper Motor - Bipolar
  esp1 = ESP32 DevKitc V4
  U1 = 74AHCT125 [part_number=SN74AHCT125 package=dil14]
  J2 = Power Jack [package=power_jack_smd]
  C1 = Electrolytic Capacitor [capacitance=0.1mF voltage=35V package="100 mil [THT, electrolytic]"]
  Mod1 = YL-99 Limit switch and LED
  Mod2 = YL-99 Limit switch and LED
  Mod3 = KY-019 5V Relay Module [package="Breakout board"]
  J3 = Power Jack [package=power_jack_smd]  # not connected
  J4 = Basic Servo

nets:
  N1: M1.PE9, J4.pulse
  GND: M1.GND-13, M1.GND-24, M1.GND-50, M1.GND-99, Pololu_A1.GND#8, esp1.IO15, esp1.GND, U1.1OE, U1.GND, Mod1.GND, Mod2.GND, Mod3.-
  N2: M1.PA3, esp1.TX
  N3: M1.PA1, Pololu_A1.DIR
  N4: M1.PA4, M1.PA2, esp1.RX
  N5: M1.PC10, Mod1.OUT
  N6: M1.PE0, U1.1A
  N7: M1.PA15, Pololu_A1.STEP
  N8: M1.PC11, Mod2.OUT
  VCC: M1.3V-97, Pololu_A1.VDD, Mod1.VCC, Mod2.VCC
  N9: M1.5V-98, U1.VCC, Mod3.+
  N10: Pololu_A1.RESET, Pololu_A1.SLEEP
  N11: Pololu_A1.1B, M2.D
  N12: Pololu_A1.1A, M2.B
  N13: Pololu_A1.2A, M2.C
  N14: Pololu_A1.2B, M2.A
  N15: Pololu_A1.GND#14, J2.GND, C1.-
  N16: Pololu_A1.VMOT, J2.GNDBREAK, C1.+
  N17: U1.1Y, Mod3.S

notes:
  External 12V Power
  External 5V Power
  Debouncer #1
  Debouncer #2
  Trigger mechanism

custom parts:
  STM32407VG Discovery: The STM32F4DISCOVERY Discovery kit allows users to easily develop applications with the STM32F407VG high performance microcontroller with the ARM® Cortex®-M4 32-bit core. It includes everything required either for beginners or for experienced users to get quickly started.Based on STM32F407VG, it includes an ST-LINK/V2 or ST-LINK/V2-A embedded debug tool, two ST-MEMS digital accelerometers, a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
  ESP32 DevKitc V4: ESP32-DevKitC board with ESP32-WROOM-32 module. ESP32-DevKitC V4 is a small-sized ESP32-based development board produced by Espressif. Most of the pins on the ESP module are broken out to the pin headers on the board. The pins D0, D1, D2, D3, CMD and CLK are used internally for communication between ESP32 and SPI flash memory. They are grouped on both sides near the USB connector. Avoid using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
  74AHCT125: Quad Level-Shifter (3V to 5V) Quadruple Bus Buffer Gates With 3-State Outputs
  KY-019 5V Relay Module: KY-019 5V Relay module, used to control AC circuits. (Special thanks to vanepp for fixing the PCB holes and other errors)
